// Logisim project Advanced.circ as structural Verilog: 1 circuit, main circuit main
module main (
  input  [2:0] Sensor_Input,
  input  [1:0] Manual_ip,
  input  Override,
  input  Ignition,
  input  [7:0] Duration_Control,
  output [1:0] Headlights
);

  wire and_1_out, and_2_out, Clock_out, multiplexer_1_out, multiplexer_2_out, not_1_out, not_2_out,
       not_3_out, not_4_out, or_1_out, or_2_out;
  wire [1:0] adder_1_out, adder_2_out, shift_register_2_q0, shift_register_2_q1, shift_register_2_q2,
       shift_register_2_q3;
  wire [2:2] adder_1_cout, adder_2_cout;
  wire [3:0] adder_3_out;
  wire [7:0] counter_1_q;

  not not_1 (not_1_out, Override);
  Clock Clock (.out(Clock_out));
  Shift_Register #(.length(4)) shift_register_1 (
    .shift(1'b1), .in(Sensor_Input[2]), .clk(and_1_out), .load(1'b0), .clr(1'b0), .d0(1'b0),
    .q0(shift_register_2_q0[1]), .d1(1'b0), .q1(shift_register_2_q1[1]), .d2(1'b0),
    .q2(shift_register_2_q2[1]), .d3(1'b0), .q3(shift_register_2_q3[1]));  // open: out
  Shift_Register #(.length(4)) shift_register_2 (
    .shift(1'b1), .in(Sensor_Input[1]), .clk(and_1_out), .load(1'b0), .clr(1'b0), .d0(1'b0),
    .q0(shift_register_2_q0[0]), .d1(1'b0), .q1(shift_register_2_q1[0]), .d2(1'b0),
    .q2(shift_register_2_q2[0]), .d3(1'b0), .q3(shift_register_2_q3[0]));  // open: out
  and and_1 (and_1_out, Clock_out, not_1_out, or_1_out);
  and and_2 (and_2_out, Clock_out, not_1_out, or_1_out);
  not not_2 (not_2_out, Ignition);
  // Probe on counter_1_q
  Counter counter_1 (
    .load(1'b1), .D(Duration_Control), .count(not_2_out), .Q(counter_1_q), .clk(and_2_out), .clr(1'b0));  // open: carry
  or or_1 (or_1_out, Ignition, counter_1_q[7], counter_1_q[6], counter_1_q[5], counter_1_q[4], counter_1_q[3], counter_1_q[2], counter_1_q[1], counter_1_q[0]);
  Adder #(.width(2)) adder_1 (
    .a(shift_register_2_q0), .b(shift_register_2_q1), .out(adder_1_out), .cin(1'b0), .cout(adder_1_cout[2]));
  Adder #(.width(2)) adder_2 (
    .a(shift_register_2_q2), .b(shift_register_2_q3), .out(adder_2_out), .cin(1'b0), .cout(adder_2_cout[2]));
  Multiplexer #(.disabled(0), .enable("false")) multiplexer_1 (
    .in0(not_4_out), .in1(Manual_ip[1]), .out(multiplexer_1_out), .sel(Override));
  Multiplexer #(.disabled(0), .enable("false")) multiplexer_2 (
    .in0(not_3_out), .in1(Manual_ip[0]), .out(multiplexer_2_out), .sel(Override));
  or or_2 (or_2_out, Override, or_1_out);
  Adder #(.width(4)) adder_3 (
    .a({1'b0, adder_1_cout[2], adder_1_out}), .b({1'b0, adder_2_cout[2], adder_2_out}), .out(adder_3_out),
    .cin(1'b0));  // open: cout
  and and_3 (Headlights[1], multiplexer_1_out, or_2_out);
  and and_4 (Headlights[0], or_2_out, multiplexer_2_out);
  not not_3 (not_3_out, adder_3_out[2]);
  not not_4 (not_4_out, adder_3_out[3]);

  // Notes on the sheet:
  //   A
  //   B
  //   C
  //   D
  //   Sum(A, B, C, D)
endmodule
