// Logisim project Basic.circ as structural Verilog: 2 circuits, main circuit main
module main (
  input  Override,
  input  [1:0] Manual,
  input  [2:0] Sensor,
  output [1:0] Headlights
);

  wire not_1_out;

  not not_1 (not_1_out, Sensor[2]);
  Multiplexer #(.enable("false")) multiplexer_1 (.in0(not_1_out), .in1(Manual[1]), .out(Headlights[1]), .sel(Override));
  Multiplexer #(.enable("false")) multiplexer_2 (.in0(Sensor[1]), .in1(Manual[0]), .out(Headlights[0]), .sel(Override));
endmodule

module Pin_out (
  input  Override,
  input  [1:0] Manual,
  input  [2:0] Sensor,
  output [1:0] Headlights
);

  wire n7404_1_p3;

  // _7404 7404_1: pin names not known; wires that end beside it: 1'b0, Sensor[2], n7404_1_p3, 1'b0, 1'b0, 1'b1, 1'b0, 1'b0, 1'b0
  // _74157 74157_1: pin names not known; wires that end beside it: Override, n7404_1_p3, Manual[1], Headlights[1], Sensor[1], Manual[0], Headlights[0], 1'b0, 1'b1, 1'b0, 1'b0, 1'b0, 1'b0, 1'b0
endmodule
